// Digital circuit 74hc243.dig as structural Verilog
module _74hc243 (
  input  A0,
  input  B0,
  input  A1,
  input  B1,
  input  A2,
  input  B2,
  input  A3,
  input  B3,
  input  VCC,
  input  GND,
  input  nOEA,
  input  OEB,
  input  NC1,
  input  NC2
);

  wire and_1_out, and_2_out;

  PowerSupply powersupply_1 (.VDD(VCC), .GND(GND));
  PullDown pulldown_1 (.out(NC1));
  PullDown pulldown_2 (.out(NC2));
  and and_1 (and_1_out, ~nOEA, ~OEB);  // And
  and and_2 (and_2_out, nOEA, OEB);
  assign B0 = and_1_out ? A0 : 1'bz;  // Driver driver_1
  assign B1 = and_1_out ? A1 : 1'bz;  // Driver driver_2
  assign B2 = and_1_out ? A2 : 1'bz;  // Driver driver_3
  assign B3 = and_1_out ? A3 : 1'bz;  // Driver driver_4
  assign A0 = and_2_out ? B0 : 1'bz;  // Driver driver_5
  assign A1 = and_2_out ? B1 : 1'bz;  // Driver driver_6
  assign A2 = and_2_out ? B2 : 1'bz;  // Driver driver_7
  assign A3 = and_2_out ? B3 : 1'bz;  // Driver driver_8

  // Notes on the sheet:
  //   A0: pin 3
  //   B0: pin 11
  //   A1: pin 4
  //   B1: pin 10
  //   A2: pin 5
  //   B2: pin 9
  //   A3: pin 6
  //   B3: pin 8
  //   VCC: pin 14, default 1
  //   GND: pin 7
  //   nOEA: pin 1
  //   OEB: pin 13
  //   NC1: pin 2
  //   NC2: pin 12
endmodule
