// Digital circuit AS6C1008.dig as structural Verilog
module AS6C1008 (
  input  A0,
  input  A1,
  input  A2,
  input  A3,
  input  A4,
  input  A5,
  input  A6,
  input  A7,
  input  A8,
  input  A9,
  input  A10,
  input  A11,
  input  A12,
  input  nCE,
  input  nOE,
  input  nWE,
  input  VCC,
  input  GND,
  input  A13,
  input  A14,
  input  A15,
  input  A16,
  input  CE2,
  output D0,
  output D1,
  output D2,
  output D3,
  output D4,
  output D5,
  output D6,
  output D7
);

  wire nand_1_out, nor_1_out;
  wire [7:0] ramsingleportsel_d;

  PowerSupply powersupply_1 (.VDD(VCC), .GND(GND));
  nand nand_1 (nand_1_out, CE2, ~nCE);  // NAnd
  RAMSinglePortSel #(.AddrBits(17), .Bits(8)) ramsingleportsel (
    .A({A16, A15, A14, A13, A12, A11, A10, A9, A8, A7, A6, A5, A4, A3, A2, A1, A0}), .CS(~nand_1_out),
    .WE(~nWE), .OE(~nOE), .D(ramsingleportsel_d));
  nor nor_1 (nor_1_out, nand_1_out, ~nWE, nOE);  // NOr
  BusSplitter #(.Bits(8)) bussplitter_1 (
    .D(ramsingleportsel_d), .OE(nor_1_out), .D0(D0), .D1(D1), .D2(D2), .D3(D3), .D4(D4), .D5(D5), .D6(D6),
    .D7(D7));

  // Notes on the sheet:
  //   A0: pin 12
  //   A1: pin 11
  //   A2: pin 10
  //   A3: pin 9
  //   A4: pin 8
  //   A5: pin 7
  //   A6: pin 6
  //   A7: pin 5
  //   A8: pin 27
  //   A9: pin 26
  //   A10: pin 23
  //   A11: pin 25
  //   A12: pin 4
  //   nCE: pin 22, default 1
  //   nOE: pin 24, default 1
  //   nWE: pin 29, default 1
  //   D0: pin 13
  //   D1: pin 14
  //   D2: pin 15
  //   D3: pin 17
  //   D4: pin 18
  //   D5: pin 19
  //   D6: pin 20
  //   D7: pin 21
  //   VCC: pin 32, default 1
  //   GND: pin 16
  //   A13: pin 28
  //   A14: pin 3
  //   A15: pin 31
  //   A16: pin 2
  //   CE2: pin 30
endmodule
