// Digital circuit chipset 2.0.dig as structural Verilog
module chipset_2_0 (
  input  [15:0] Add__Bus,
  input  niognt_m,
  input  HALT,
  input  [2:0] bank,
  input  bank_clk,
  input  nxsin_in,
  input  rnw,
  input  e,
  input  in_9,
  output \wait ,
  output nioreq,
  output nxsin
);

  wire HALT_t, mrdy, nand_3_out, nbioreq, ncpu, nres_out, RA14, RA15, RA16, rd, rd_b, res,
       U3___R__W___UPPER_ADDRES_SELECTION_pin11, U3___R__W___UPPER_ADDRES_SELECTION_pin12, wr, wr_b, xsin;

  PullUp pullup_1 (.out(nxsin_in));
  nand nand_1 (HALT_t, HALT, HALT);
  Reset nres (.out(nres_out));
  not not_1 (res, nres_out);
  nand nand_2 (xsin, nxsin_in, nxsin_in);
  _74138 ADDRESS_DEC (
    .pin1(Add__Bus[12]), .pin2(Add__Bus[13]), .pin3(Add__Bus[14]), .pin4(1'b0), .pin5(1'b0),
    .pin6(Add__Bus[15]), .pin8(1'b0), .pin13(nioreq), .pin16(1'b1));  // open: pin7, pin9, pin10, pin11, pin12, pin14, pin15
  _74139 U3___R__W___UPPER_ADDRES_SELECTION (
    .pin1(in_9), .pin2(rnw), .pin3(e), .pin6(wr), .pin7(rd), .pin8(1'b0),
    .pin11(U3___R__W___UPPER_ADDRES_SELECTION_pin11), .pin12(U3___R__W___UPPER_ADDRES_SELECTION_pin12),
    .pin13(Add__Bus[14]), .pin14(Add__Bus[13]), .pin15(Add__Bus[15]), .pin16(1'b1));  // open: pin4, pin5, pin9, pin10
  nand nand_3 (nand_3_out, nioreq, nioreq);
  DiodeBackward diodebackward_1 (.in(U3___R__W___UPPER_ADDRES_SELECTION_pin12), .out(ncpu));
  PullUp pullup_2 (.out(ncpu));
  DiodeBackward diodebackward_2 (.in(U3___R__W___UPPER_ADDRES_SELECTION_pin11), .out(ncpu));
  nand nand_4 (\wait , nand_3_out, niognt_m);
  _74173 address_reg (
    .pin1(ncpu), .pin2(1'b0), .pin3(RA14), .pin4(RA15), .pin5(RA16), .pin7(bank_clk), .pin8(1'b0),
    .pin9(1'b0), .pin10(1'b0), .pin11(1'b0), .pin12(bank[2]), .pin13(bank[1]), .pin14(bank[0]), .pin15(res),
    .pin16(1'b1));  // open: pin6
  PullUp pullup_3 (.out(wr_b));
  PullUp pullup_4 (.out(rd_b));
  PullUp pullup_5 (.out(HALT_t));
  _74125 _74125_1 (
    .pin1(HALT_t), .pin2(wr), .pin3(wr_b), .pin4(HALT_t), .pin5(rd), .pin6(rd_b), .pin7(1'b0), .pin8(mrdy),
    .pin9(\wait ), .pin10(res), .pin11(nbioreq), .pin12(nioreq), .pin13(xsin), .pin14(1'b1));
  _74hc243 non_bank_address (
    .A0(RA14), .B0(Add__Bus[14]), .A1(RA15), .B1(Add__Bus[15]), .A2(RA16), .B2(1'b0), .B3(1'b0), .VCC(1'b1),
    .GND(1'b0), .nOEA(ncpu), .OEB(1'b1));  // open: A3, NC1, NC2
  PullUp pullup_6 (.out(res));

  assign nxsin = nxsin_in;

  // Other names for the same wires on the sheet: A10 = Add__Bus[10]; A11 = Add__Bus[11]; A12 = Add__Bus[12];
  //   A13 = Add__Bus[13]; A14 = Add__Bus[14]; A15 = Add__Bus[15]; badd = bank_clk; d0 = bank[0]; d1 = bank[1];
  //   d2 = bank[2]; nHALT = HALT; niognt = niognt_m
endmodule
