// Digital circuit chipset.dig as structural Verilog
module chipset (
  input  [15:0] Add__Bus,
  input  niognt_m,
  input  HALT,
  input  rnw,
  input  e,
  input  in_10,
  input  [2:0] bank,
  input  bank_clk,
  input  in_13,
  output nram,
  output nrom,
  output nioreq,
  output \wait 
);

  wire ADDRESS_DEC_pin12, ADDRESS_DEC_pin14, ADDRESS_DEC_pin15, and_1_out, HALT_t, mrdy, nand_1_out, nbioreq,
       ncpu, not_3_out, nres_out, RA14, RA15, RA16, rd, res, U3___R__W___UPPER_ADDRES_SELECTION_pin11,
       U3___R__W___UPPER_ADDRES_SELECTION_pin12, wr, wr_b;

  Reset nres (.out(nres_out));
  not not_1 (HALT_t, HALT);
  not not_2 (res, nres_out);
  _74138 ADDRESS_DEC (
    .pin1(Add__Bus[12]), .pin2(Add__Bus[13]), .pin3(Add__Bus[14]), .pin4(1'b0), .pin5(1'b0),
    .pin6(Add__Bus[15]), .pin8(1'b0), .pin12(ADDRESS_DEC_pin12), .pin13(nioreq), .pin14(ADDRESS_DEC_pin14),
    .pin15(ADDRESS_DEC_pin15), .pin16(1'b1));  // open: pin7, pin9, pin10, pin11
  _74139 U3___R__W___UPPER_ADDRES_SELECTION (
    .pin1(in_10), .pin2(rnw), .pin3(e), .pin6(wr), .pin7(rd), .pin8(1'b0),
    .pin11(U3___R__W___UPPER_ADDRES_SELECTION_pin11), .pin12(U3___R__W___UPPER_ADDRES_SELECTION_pin12),
    .pin13(Add__Bus[14]), .pin14(Add__Bus[13]), .pin15(Add__Bus[15]), .pin16(1'b1));  // open: pin4, pin5, pin9, pin10
  and and_1 (and_1_out, ADDRESS_DEC_pin15, ADDRESS_DEC_pin14);
  nand nand_1 (nand_1_out, Add__Bus[14], Add__Bus[15]);
  and and_2 (ncpu, U3___R__W___UPPER_ADDRES_SELECTION_pin12, U3___R__W___UPPER_ADDRES_SELECTION_pin11);
  not not_3 (not_3_out, nioreq);
  nand nand_2 (\wait , not_3_out, niognt_m);
  and and_3 (nram, and_1_out, Add__Bus[15]);
  and and_4 (nrom, ADDRESS_DEC_pin12, nand_1_out);
  _74173 address_reg (
    .pin1(ncpu), .pin2(1'b0), .pin3(RA14), .pin4(RA15), .pin5(RA16), .pin7(bank_clk), .pin8(1'b0),
    .pin9(1'b0), .pin10(1'b0), .pin11(1'b0), .pin12(bank[2]), .pin13(bank[2]), .pin14(bank[0]), .pin15(res),
    .pin16(1'b1));  // open: pin6
  PullUp pullup_1 (.out(wr_b));
  PullUp pullup_2 (.out(wr_b));
  PullUp pullup_3 (.out(HALT_t));
  _74125 _74125_1 (
    .pin1(HALT_t), .pin2(wr), .pin3(wr_b), .pin4(HALT_t), .pin5(rd), .pin6(wr_b), .pin7(1'b0), .pin8(mrdy),
    .pin9(\wait ), .pin10(res), .pin11(nbioreq), .pin12(nioreq), .pin13(in_13), .pin14(1'b1));
  _74hc243 non_bank_address (
    .A0(RA14), .B0(Add__Bus[14]), .A1(RA15), .B1(Add__Bus[15]), .A2(RA16), .B2(1'b0), .B3(1'b0), .VCC(1'b1),
    .GND(1'b0), .nOEA(ncpu), .OEB(1'b1));  // open: A3, NC1, NC2
  PullDown pulldown_1 (.out(in_13));
  PullUp pullup_4 (.out(res));

  assign bank[1] = bank[2];

  // Other names for the same wires on the sheet: A10 = Add__Bus[10]; A11 = Add__Bus[11]; A12 = Add__Bus[12];
  //   A13 = Add__Bus[13]; A14 = Add__Bus[14]; A15 = Add__Bus[15]; badd = bank_clk; d0 = bank[0]; d2 = bank[2];
  //   nHALT = HALT; niognt = niognt_m; xsin = in_13
endmodule
